# Fritzing sketch RitmoCardiaco (saved by Fritzing 0.9.6b)
breadboards: 1

parts:
  Mod1 = Raspberry Pi Pico
  LED1 = RGB LED (com. cathode, rbg) [package="5 mm [THT]"]
  SEN1 = Pulse Sensor [package=SIP-3]

nets:
  N1: Mod1.pin_1, LED1.green_anode
  N2: Mod1.pin_2, LED1.blue_anode
  N3: Mod1.pin_3, Mod1.pin_8, Mod1.pin_13, Mod1.pin_18, Mod1.pin_23, Mod1.pin_28, Mod1.pin_33, Mod1.pin_38, Mod1.pin_42, LED1.common_cathode, SEN1.GND
  N4: Mod1.pin_4, LED1.red_anode
  N5: Mod1.pin_31, SEN1.Signal
  N6: Mod1.pin_36, SEN1.VCC

custom parts:
  Raspberry Pi Pico: Raspberry Pi Pico. Based around the RP2040 microcontroller the Pico is a low cost microcontroller device bringing Raspberry Pi quality, cost, and easy of use to the microcontroller space. Jan 2021, Split part in to two versions: tht (this one) and SMD. This one will drill holes for a .1 in header in pcb to allow plugging in the module as well as providing pads to solder the module to the top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
  Pulse Sensor: Pulse Sensor Optical Heart Beat Sensor
